// Logisim project Michael.circ as structural Verilog: 6 circuits, main circuit main
module main (
);

  wire clock_1_out, ex_mem_1_regwriteout, execute_1_regwriteout, memory_1_regwriteout;
  wire [4:0] ex_mem_1_rwout, execute_1_rwout, memory_1_rwout;
  wire [31:0] ex_mem_1_alures_out, ex_mem_1_pcout, execute_1_aluoutput, execute_1_pcout, memory_1_alures_out,
       memory_1_pcout;

  Clock clock_1 (.out(clock_1_out));
  Execute execute_1 (
    .ALUoutput(execute_1_aluoutput), .RegWriteOut(execute_1_regwriteout), .rWout(execute_1_rwout),
    .PCout(execute_1_pcout));  // open: A, B, Funct30, Sa, Op, RegWriteIn, rW, PC
  EX_MEM ex_mem_1 (
    .ALUres_in(execute_1_aluoutput), .RegWrite(execute_1_regwriteout), .rW(execute_1_rwout),
    .PC(execute_1_pcout), .clock(clock_1_out), .ALUres_out(ex_mem_1_alures_out),
    .RegWriteOut(ex_mem_1_regwriteout), .rWout(ex_mem_1_rwout), .PCout(ex_mem_1_pcout));
  Memory memory_1 (
    .ALUres_in(ex_mem_1_alures_out), .RegWriteIn(ex_mem_1_regwriteout), .rW(ex_mem_1_rwout),
    .PC(ex_mem_1_pcout), .ALUres_out(memory_1_alures_out), .RegWriteOut(memory_1_regwriteout),
    .rWout(memory_1_rwout), .PCout(memory_1_pcout));
  MEM_WB mem_wb_1 (
    .ALUres_in(memory_1_alures_out), .RegWriteIn(memory_1_regwriteout), .rW(memory_1_rwout),
    .PC(memory_1_pcout), .clock(clock_1_out));  // open: ALUres_out, RegWriteOut, rWout, PCout
endmodule

module Execute (
  input  [31:0] A,
  input  [31:0] B,
  input  Funct30,
  input  [4:0] Sa,
  input  [3:0] Op,
  input  RegWriteIn,
  input  [4:0] rW,
  input  [31:0] PC,
  output [31:0] ALUoutput,
  output RegWriteOut,
  output [4:0] rWout,
  output [31:0] PCout
);

  wire [31:0] alu_1_p6;

  // ALU alu_1: pin names not known; wires that end beside it: Funct30, A, B, Op, Sa, alu_1_p6
  ALUresult aluresult_1 (
    .A(A), .B(B), .C(alu_1_p6), .Funct30(Funct30), .Op0(Op[0]), .Op1(Op[1]), .RegWriteIn(RegWriteIn),
    .ALUoutput(ALUoutput), .RegWriteOut(RegWriteOut));

  assign PCout = PC;
  assign rWout = rW;
endmodule

module ALUresult (
  input  [31:0] A,
  input  [31:0] B,
  input  [31:0] C,
  input  Funct30,
  input  Op0,
  input  Op1,
  input  RegWriteIn,
  output [31:0] ALUoutput,
  output RegWriteOut
);

  wire comparator_1_lt, comparator_2_lt;
  wire [31:0] bit_extender_1_out, bit_extender_2_out, multiplexer_1_out, multiplexer_2_out;

  Comparator #(.width(32)) comparator_1 (.a(A), .b(B), .lt(comparator_1_lt));  // open: gt, eq
  Comparator #(.width(32), .mode("unsigned")) comparator_2 (.a(A), .b(B), .lt(comparator_2_lt));  // open: gt, eq
  assign bit_extender_1_out = {{31{1'b0}}, comparator_1_lt};  // Bit_Extender bit_extender_1
  assign bit_extender_2_out = {{31{1'b0}}, comparator_2_lt};  // Bit_Extender bit_extender_2
  Multiplexer #(.width(32), .enable("false")) multiplexer_1 (
    .in0(bit_extender_1_out), .in1(bit_extender_2_out), .out(multiplexer_1_out), .sel(Funct30));
  Multiplexer #(.width(32), .enable("false")) multiplexer_2 (
    .in0(multiplexer_1_out), .in1(C), .out(multiplexer_2_out), .sel(Op0));
  Multiplexer #(.width(32), .enable("false")) multiplexer_3 (
    .in0(multiplexer_2_out), .in1(C), .out(ALUoutput), .sel(Op1));

  assign RegWriteOut = RegWriteIn;
endmodule

module EX_MEM (
  input  [31:0] ALUres_in,
  input  RegWrite,
  input  [4:0] rW,
  input  [31:0] PC,
  input  clock,
  output [31:0] ALUres_out,
  output RegWriteOut,
  output [4:0] rWout,
  output [31:0] PCout
);

  Register #(.width(32)) register_1 (.D(ALUres_in), .clk(clock), .Q(ALUres_out));  // open: en, clr
  Register #(.width(1)) register_2 (.D(RegWrite), .clk(clock), .Q(RegWriteOut));  // open: en, clr
  Register #(.width(5)) register_3 (.D(rW), .clk(clock), .Q(rWout));  // open: en, clr
  Register #(.width(32)) register_4 (.D(PC), .clk(clock), .Q(PCout));  // open: en, clr
endmodule

module Memory (
  input  [31:0] ALUres_in,
  input  RegWriteIn,
  input  [4:0] rW,
  input  [31:0] PC,
  output [31:0] ALUres_out,
  output RegWriteOut,
  output [4:0] rWout,
  output [31:0] PCout
);


  assign ALUres_out = ALUres_in;
  assign PCout = PC;
  assign RegWriteOut = RegWriteIn;
  assign rWout = rW;
endmodule

module MEM_WB (
  input  [31:0] ALUres_in,
  input  RegWriteIn,
  input  [4:0] rW,
  input  [31:0] PC,
  input  clock,
  output [31:0] ALUres_out,
  output RegWriteOut,
  output [4:0] rWout,
  output [31:0] PCout
);

  Register #(.width(32)) register_1 (.D(ALUres_in), .clk(clock), .Q(ALUres_out));  // open: en, clr
  Register #(.width(1)) register_2 (.D(RegWriteIn), .clk(clock), .Q(RegWriteOut));  // open: en, clr
  Register #(.width(5)) register_3 (.D(rW), .clk(clock), .Q(rWout));  // open: en, clr
  Register #(.width(32)) register_4 (.D(PC), .clk(clock), .Q(PCout));  // open: en, clr
endmodule
